// Logisim project Divyank_7_segment.circ as structural Verilog: 1 circuit, main circuit main
module main (
  input  A,
  input  B,
  input  C,
  input  D
);

  wire A_2_out, a_out, b_out, B_prime_C_out, B_prime_D_out, B_prime_D_prime_out, BC_prime_D_out,
       BD_prime_out, c_out, C_prime_D_prime_out, CD_out, CD_prime_out, d_out, e_out, f_out, g_out, not_1_out,
       not_2_out, not_3_out, not_4_out;

  and B_prime_D_prime (B_prime_D_prime_out, not_2_out, not_4_out);
  or u_a (a_out, BC_prime_D_out, A_2_out, B_prime_C_out, BD_prime_out);
  and B_prime_D (B_prime_D_out, not_2_out, D);
  and B_prime_C (B_prime_C_out, not_2_out, C);
  or u_b (b_out, BD_prime_out, C_prime_D_prime_out, BC_prime_D_out, A_2_out);
  not not_1 (not_1_out, A);
  and CD_prime (CD_prime_out, C, not_4_out);
  not not_2 (not_2_out, B);
  or u_c (c_out, CD_out, BC_prime_D_out, A_2_out, B_prime_D_prime_out, CD_prime_out);
  not not_3 (not_3_out, C);
  _7_Segment_Display u_7_segment_display_1 (
    .g(a_out), .f(b_out), .a(c_out), .b(d_out), .e(e_out), .d(f_out), .c(g_out));  // open: dp
  and BD_prime (BD_prime_out, B, not_4_out);
  or u_d (d_out, B_prime_D_out, C_prime_D_prime_out, CD_out, B_prime_C_out);
  not not_4 (not_4_out, D);
  and C_prime_D_prime (C_prime_D_prime_out, not_3_out, not_4_out);
  and CD (CD_out, C, D);
  or e (e_out, B_prime_D_prime_out, CD_prime_out);
  and BC_prime_D (BC_prime_D_out, B, not_3_out, D);
  or f (f_out, BC_prime_D_out, A_2_out, B_prime_D_prime_out, B_prime_C_out, CD_prime_out);
  buf A_2 (A_2_out, A);  // AND_Gate
  or g (g_out, B_prime_D_out, BD_prime_out, C_prime_D_prime_out, CD_out, BC_prime_D_out);
endmodule
