// Logisim project Divyank_Sharma_Part_B_Latch.circ as structural Verilog: 1 circuit, main circuit main
module main (
  input  in_1,
  input  in_2,
  input  C,
  input  D,
  input  C_2,
  input  D_2,
  output Q,
  output Q_prime,
  output Q_2,
  output Q_prime_2,
  output Q_3,
  output Q_prime_3
);

  wire and_1_out, and_2_out, and_3_out, and_4_out, and_5_out, and_6_out, nor_5_out, nor_6_out, not_1_out,
       not_2_out, not_3_out, not_4_out;

  not not_1 (not_1_out, D);
  not not_2 (not_2_out, D_2);
  and and_1 (and_1_out, C, not_1_out);
  and and_2 (and_2_out, C, D);
  and and_3 (and_3_out, C_2, not_2_out);
  and and_4 (and_4_out, C_2, D_2);
  nor nor_1 (Q, in_1, Q_prime);
  nor nor_2 (Q_prime, Q, in_2);
  nor nor_3 (Q_2, and_1_out, Q_prime_2);
  nor nor_4 (Q_prime_2, Q_2, and_2_out);
  nor nor_5 (nor_5_out, and_3_out, nor_6_out);
  nor nor_6 (nor_6_out, nor_5_out, and_4_out);
  not not_3 (not_3_out, C_2);
  not not_4 (not_4_out, nor_5_out);
  and and_5 (and_5_out, not_3_out, not_4_out);
  and and_6 (and_6_out, not_3_out, nor_5_out);
  nor nor_7 (Q_3, and_5_out, Q_prime_3);
  nor nor_8 (Q_prime_3, Q_3, and_6_out);

  // Notes on the sheet:
  //   Reset
  //   Set
  //   Latch
  //   D-Latch
  //   A D Flip Flop with a falling-edge 
  //   DIVYANK SHARMA PART-B ASSIGNMENT 2
  //   Q
endmodule
